# Fritzing sketch c5 (saved by Fritzing 0.9.3b)
breadboards: 1

parts:
  Raspberry_Pi_1 = Raspberry Pi 3 [part_number=RPI-3-V1.2]
  R4 = Resistor [tolerance=±5% resistance=220 package=THT]
  LED3 = LED - 5mm [color="Red (633nm)" package="5 mm [THT]"]
  S2 = Pushbutton [package="[THT]"]
  S3 = Pushbutton [package="[THT]"]

nets:
  N1: Raspberry_Pi_1.GPIO4, LED3.anode
  N2: Raspberry_Pi_1.GND, R4.Pin_0, S2.Pin_1, S2.Pin_2, S3.Pin_3, S3.Pin_4
  N3: Raspberry_Pi_1.GPIO15, S2.Pin_3, S2.Pin_4
  N4: Raspberry_Pi_1.GPIO14, S3.Pin_1, S3.Pin_2
  N5: R4.Pin_1, LED3.cathode

notes:
  Circuito 5
